# Fritzing sketch robotito_bluetooth (saved by Fritzing 0.9.3b)

parts:
  M1 = BTS7960
  part = Arduino Nano (Rev3.0)
  U1 = LIPO-2000mAh [package=lipo-2000]
  MotorA = DC Motor
  part_2 = L298_BRIDGE_DRIVER [package=powerso20]
  MotorB = DC Motor
  U3 = LIPO-2000mAh [package=lipo-2000]
  part_3 = Bluetooth HC-06u [package=THT]
  S1 = SPST Switch [package=switch-spdt]
  S2 = SPST Switch [package=switch-spdt]
  Weapon = DC Motor
  Fan = Fan - Ventilador [package=THT]

nets:
  N1: M1.pin1, part.D10
  N2: M1.pin2, part.D9
  N3: M1.pin3, part.D7
  N4: M1.pin4, part.D8
  N5: M1.pin7, part.5V
  GND: M1.pin8, part.GND, part_2.GND, U3.-, part_3.GND
  N6: M1.pin9, Weapon.pin_1
  N7: M1.pin10, Weapon.pin_2
  N8: M1.pin11, S2.S, Fan.5V
  N9: M1.pin12, U1.-, Fan.GND
  N10: part.D2, part_2.IN1
  N11: part.D3, part_2.ENA
  N12: part.D4, part_2.IN2
  N13: part.D5, part_3.RXD
  N14: part.D6, part_3.TXD
  N15: part.D11/MOSI, part_2.ENB
  N16: part.D12/MISO, part_2.IN4
  VIN: part.VIN, part_2.VSS
  3V3: part.3V3, part_3.VCC
  N17: part.D13/SCK, part_2.IN3
  N18: U1.+, S2.P
  N19: MotorA.pin_1, part_2.OUT2
  N20: MotorA.pin_2, part_2.OUT1
  N21: part_2.VS, S1.O
  N22: part_2.OUT3, MotorB.pin_1
  N23: part_2.OUT4, MotorB.pin_2
  N24: U3.+, S1.P

custom parts:
  BTS7960: BTS7960 43A Peak Power H-Bridge PWM Motor Driver
  Bluetooth HC-06u: Bluetooth HC-06 - face up, pins down 16.5mm x 37.5mm PCB
  Fan - Ventilador: Ventilador de 2 pines, se encuentra comunmente en computadoras de escritorio
